# Fritzing sketch 1st (saved by Fritzing 0.9.0b)
circuit board: 8.46667cm x 5.64444cm
breadboards: 1

parts:
  JP3 = Header 1 [package=1x01_offset]
  JP4 = Header 1 [package=1x01_offset]
  JP5 = Header 1 [package=1x01_offset]
  JP7 = Header 1 [package=1x01_offset]
  JP6 = Header 1 [package=1x01_offset]
  12V+ = Header 1 [package=1x01_offset]
  12V- = Header 1 [package=1x01_offset]
  IC1 = ULN2003A [package="DIP16 [THT]"]
  Part1 = Arduino Uno (Rev3)

nets:
  N1: JP3.1, IC1.Out_2
  N2: JP4.1, 12V+.1, IC1.COM_-_Common
  N3: JP5.1, IC1.Out_3
  N4: JP7.1, IC1.Out_1
  N5: JP6.1, IC1.Out_4
  N6: 12V-.1, IC1.0V, Part1.GND
  N7: IC1.In_1, Part1.D11_PWM/MOSI
  N8: IC1.In_2, Part1.D10_PWM/SS
  N9: IC1.In_3, Part1.D9_PWM
  N10: IC1.In_4, Part1.D8
